# Fritzing sketch Receiver (saved by Fritzing 0.9.3b)

parts:
  U1 = XD-RF-5V [package=THT]
  Bauteil3 = Arduino Nano (Rev3.0)

nets:
  VCC: U1.VCC, Bauteil3.RESET, Bauteil3.5V
  N1: U1.DATA, Bauteil3.D10, Bauteil3.D11/MOSI
  GND: U1.GND, Bauteil3.GND

custom parts:
  XD-RF-5V: This is 433Mhz RF transmitter with receiver kit for Arduino ARM MCU wireless Application environment: Remote control switch, receiver module, motorcycles, automobile anti-theft products, home security products, electric doors, shutter doors, windows, remote control socket, remote control LED, remote audio remote control electric doors, garage door remote control, remote control retractable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
